// Logisim project circuito.circ as structural Verilog: 4 circuits, main circuit project_reti_logiche
module project_reti_logiche (
  input  i_done_internal,
  input  i_rst,
  input  i_start,
  input  i_w,
  input  r19_load,
  input  r18_load,
  input  r17_load,
  input  r1_load,
  input  r16_load,
  input  r15__load,
  input  r2_load,
  input  r14_load,
  input  r13_load,
  input  r12_load,
  input  r11_load,
  input  r10_load,
  input  r9_load,
  input  r8_load,
  input  r7_load,
  input  r6_load,
  input  r5_load,
  input  r4_load,
  input  r3_load,
  input  o_mem_we,
  input  ready_load,
  input  o_mem_en,
  output o_done,
  output [7:0] o_z0,
  output [7:0] o_z1,
  output [7:0] o_z2,
  output [7:0] o_z3
);

  wire i_clk_out;
  wire [1:0] shift_reg_2_1_o_reg1;
  wire [7:0] ram_1_data;
  wire [15:0] shift_reg_16_reverse_1_out_21;

  Clock i_clk (.out(i_clk_out));
  shift_reg_2 shift_reg_2_1 (
    .r1_load(r1_load), .r2_load(r2_load), .i_w(i_w), .i_rst(i_clk_out), .o_reg1(shift_reg_2_1_o_reg1[0]),
    .o_reg2(shift_reg_2_1_o_reg1[1]));
  RAM #(.addrWidth(16), .bus("separate")) ram_1 (
    .addr(shift_reg_16_reverse_1_out_21), .data(ram_1_data), .str(o_mem_we), .clk(i_clk_out), .ld(o_mem_en));  // open: din, sel, clr
  shift_reg_16_reverse shift_reg_16_reverse_1 (
    .out_21(shift_reg_16_reverse_1_out_21[0]), .out_22(shift_reg_16_reverse_1_out_21[1]),
    .out_23(shift_reg_16_reverse_1_out_21[2]), .out_24(shift_reg_16_reverse_1_out_21[3]),
    .out_25(shift_reg_16_reverse_1_out_21[4]), .out_26(shift_reg_16_reverse_1_out_21[5]),
    .out_27(shift_reg_16_reverse_1_out_21[6]), .out_28(shift_reg_16_reverse_1_out_21[7]),
    .out_29(shift_reg_16_reverse_1_out_21[8]), .out_30(shift_reg_16_reverse_1_out_21[9]),
    .out_31(shift_reg_16_reverse_1_out_21[10]), .out_32(shift_reg_16_reverse_1_out_21[11]),
    .out_33(shift_reg_16_reverse_1_out_21[12]), .out_34(shift_reg_16_reverse_1_out_21[13]),
    .out_35(shift_reg_16_reverse_1_out_21[14]), .out_36(shift_reg_16_reverse_1_out_21[15]), .i_rst(i_w),
    .i_done_internal(i_clk_out), .i_w(i_rst), .r19_load(r19_load), .r18_load(r18_load), .r17_load(r17_load),
    .r16_load(r16_load), .r15_load(r15__load), .r14_load(r14_load), .r13_load(r13_load), .r12_load(r12_load),
    .r11_load(r11_load), .r10_load(r10_load), .r9_load(r9_load), .r8_load(r8_load), .r7_load(r7_load),
    .r6_load(r6_load), .r5_load(r5_load), .r4_load(r4_load), .r3_load(r3_load));
  sorter sorter_1 (
    .data(ram_1_data), .i_done_internal(i_done_internal), .ready_load(ready_load), .i_rst(i_rst),
    .sort(shift_reg_2_1_o_reg1), .o_muxZ0(o_z0), .o_muxZ1(o_z1), .o_muxZ2(o_z2), .o_muxZ3(o_z3));

  assign o_done = i_done_internal;
endmodule

module shift_reg_2 (
  input  i_w,
  input  i_rst,
  input  r1_load,
  input  r2_load,
  output o_reg1,
  output o_reg2
);

  wire i_clk_out;

  Clock i_clk (.out(i_clk_out));
  D_Flip_Flop reg1 (.clk(i_clk_out), .D(i_w), .Q(o_reg1), .en(r1_load), .reset(i_rst));  // open: Qn, preset
  D_Flip_Flop reg2 (.clk(i_clk_out), .D(o_reg1), .Q(o_reg2), .en(r2_load), .reset(i_rst));  // open: Qn, preset
endmodule

module shift_reg_16_reverse (
  input  i_rst,
  input  i_done_internal,
  input  i_w,
  input  r19_load,
  input  r18_load,
  input  r17_load,
  input  r16_load,
  input  r15_load,
  input  r14_load,
  input  r13_load,
  input  r12_load,
  input  r11_load,
  input  r10_load,
  input  r9_load,
  input  r8_load,
  input  r7_load,
  input  r6_load,
  input  r5_load,
  input  r4_load,
  input  r3_load,
  output out_21,
  output out_22,
  output out_23,
  output out_24,
  output out_25,
  output out_26,
  output out_27,
  output out_28,
  output out_29,
  output out_30,
  output out_31,
  output out_32,
  output out_33,
  output out_34,
  output out_35,
  output out_36
);

  wire i_clk_out, or_1_out, reg19_q;

  Clock i_clk (.out(i_clk_out));
  or or_1 (or_1_out, i_rst, i_done_internal);
  D_Flip_Flop reg19 (.clk(i_clk_out), .D(i_w), .Q(reg19_q), .preset(or_1_out), .en(r19_load));  // open: Qn, reset
  D_Flip_Flop reg18 (.clk(i_clk_out), .D(reg19_q), .Q(out_21), .preset(or_1_out), .en(r18_load));  // open: Qn, reset
  D_Flip_Flop reg17 (.clk(i_clk_out), .D(out_21), .Q(out_22), .preset(or_1_out), .en(r17_load));  // open: Qn, reset
  D_Flip_Flop reg16 (.clk(i_clk_out), .D(out_22), .Q(out_23), .preset(or_1_out), .en(r16_load));  // open: Qn, reset
  D_Flip_Flop reg15 (.clk(i_clk_out), .D(out_23), .Q(out_24), .preset(or_1_out), .en(r15_load));  // open: Qn, reset
  D_Flip_Flop reg14 (.clk(i_clk_out), .D(out_24), .Q(out_25), .preset(or_1_out), .en(r14_load));  // open: Qn, reset
  D_Flip_Flop reg13 (.clk(i_clk_out), .D(out_25), .Q(out_26), .preset(or_1_out), .en(r13_load));  // open: Qn, reset
  D_Flip_Flop reg12 (.clk(i_clk_out), .D(out_26), .Q(out_27), .preset(or_1_out), .en(r12_load));  // open: Qn, reset
  D_Flip_Flop reg11 (.clk(i_clk_out), .D(out_27), .Q(out_28), .preset(or_1_out), .en(r11_load));  // open: Qn, reset
  D_Flip_Flop reg10 (.clk(i_clk_out), .D(out_28), .Q(out_29), .preset(or_1_out), .en(r10_load));  // open: Qn, reset
  D_Flip_Flop reg9 (.clk(i_clk_out), .D(out_29), .Q(out_30), .preset(or_1_out), .en(r9_load));  // open: Qn, reset
  D_Flip_Flop reg8 (.clk(i_clk_out), .D(out_30), .Q(out_31), .preset(or_1_out), .en(r8_load));  // open: Qn, reset
  D_Flip_Flop reg7 (.clk(i_clk_out), .D(out_31), .Q(out_32), .preset(or_1_out), .en(r7_load));  // open: Qn, reset
  D_Flip_Flop reg6 (.clk(i_clk_out), .D(out_32), .Q(out_33), .preset(or_1_out), .en(r6_load));  // open: Qn, reset
  D_Flip_Flop reg5 (.clk(i_clk_out), .D(out_33), .Q(out_34), .preset(or_1_out), .en(r5_load));  // open: Qn, reset
  D_Flip_Flop reg4 (.clk(i_clk_out), .D(out_34), .Q(out_35), .preset(or_1_out), .en(r4_load));  // open: Qn, reset
  D_Flip_Flop reg3 (.clk(i_clk_out), .D(out_35), .Q(out_36), .preset(or_1_out), .en(r3_load));  // open: Qn, reset
endmodule

module sorter (
  input  [7:0] data,
  input  i_done_internal,
  input  ready_load,
  input  i_rst,
  input  [1:0] sort,
  output [7:0] o_muxZ0,
  output [7:0] o_muxZ1,
  output [7:0] o_muxZ2,
  output [7:0] o_muxZ3
);

  wire and_1_out, and_2_out, and_3_out, and_4_out, demultiplexer_1_out0, demultiplexer_1_out1,
       demultiplexer_1_out2, demultiplexer_1_out3, i_clk_out;
  wire [7:0] register_1_q, register_2_q, register_3_q, register_4_q;

  Clock i_clk (.out(i_clk_out));
  Demultiplexer #(.select(2)) demultiplexer_1 (
    .out0(demultiplexer_1_out0), .out1(demultiplexer_1_out1), .out2(demultiplexer_1_out2),
    .out3(demultiplexer_1_out3), .in(1'b1), .sel(sort), .en(1'b1));
  and and_1 (and_1_out, ready_load, demultiplexer_1_out0);
  and and_2 (and_2_out, ready_load, demultiplexer_1_out1);
  and and_3 (and_3_out, ready_load, demultiplexer_1_out2);
  and and_4 (and_4_out, ready_load, demultiplexer_1_out3);
  Register register_1 (.D(data), .en(and_1_out), .Q(register_1_q), .clk(i_clk_out), .clr(i_rst));
  Register register_2 (.D(data), .en(and_2_out), .Q(register_2_q), .clk(i_clk_out), .clr(i_rst));
  Register register_3 (.D(data), .en(and_3_out), .Q(register_3_q), .clk(i_clk_out), .clr(i_rst));
  Register register_4 (.D(data), .en(and_4_out), .Q(register_4_q), .clk(i_clk_out), .clr(i_rst));
  Multiplexer #(.width(8)) multiplexer_1 (
    .in0({8{1'b0}}), .in1(register_1_q), .out(o_muxZ0), .sel(i_done_internal), .en(1'b1));
  Multiplexer #(.width(8)) multiplexer_2 (
    .in0({8{1'b0}}), .in1(register_2_q), .out(o_muxZ1), .sel(i_done_internal), .en(1'b1));
  Multiplexer #(.width(8)) multiplexer_3 (
    .in0({8{1'b0}}), .in1(register_3_q), .out(o_muxZ2), .sel(i_done_internal), .en(1'b1));
  Multiplexer #(.width(8)) multiplexer_4 (
    .in0({8{1'b0}}), .in1(register_4_q), .out(o_muxZ3), .sel(i_done_internal), .en(1'b1));
endmodule
